# Fritzing sketch Curso_Programacion-Montaje Wemos (saved by Fritzing 0.9.3b)
breadboards: 1

parts:
  WeMos_D1_Mini1 = WeMos D1 Mini
  WeMos_D1_Mini_Relay_Shield_V1 = WeMos D1 Mini Relay Shield V2
  WeMos_D1_Mini_OLED_Shield1 = WeMos D1 Mini OLED Shield
  S1 = Pushbutton [package="[THT]"]
  WeMos_D1_Mini_WS2812B_RGB_Shield1 = WeMos D1 Mini WS2812B RGB Shield

nets:
  5V: WeMos_D1_Mini1.5V, WeMos_D1_Mini_Relay_Shield_V1.5V, WeMos_D1_Mini_OLED_Shield1.5V, WeMos_D1_Mini_WS2812B_RGB_Shield1.5V
  N1: WeMos_D1_Mini1.D1, WeMos_D1_Mini_OLED_Shield1.D1
  N2: WeMos_D1_Mini1.D2, WeMos_D1_Mini_OLED_Shield1.D2
  N3: WeMos_D1_Mini1.D3, S1.Pin_1, S1.Pin_2
  N4: WeMos_D1_Mini1.D4, WeMos_D1_Mini_WS2812B_RGB_Shield1.D4
  N5: WeMos_D1_Mini1.G, WeMos_D1_Mini_Relay_Shield_V1.G, WeMos_D1_Mini_OLED_Shield1.G, S1.Pin_3, S1.Pin_4, WeMos_D1_Mini_WS2812B_RGB_Shield1.G
